# Fritzing sketch Control de 2 Relay con Arduino Leonardo (saved by Fritzing 0.9.3b)
circuit board: 8.46667cm x 5.64444cm

parts:
  Componente1 = Arduino Leonardo (Rev3b)
  Componente2 = Bluetooth HC-05 Macho
  U1 = 2-Channel 5v Relay Shield [package=relay-2ch5v10a]

nets:
  N1: Componente1.D0/RX, Componente2.TXD
  N2: Componente1.D1/TX, Componente2.RXD
  N3: Componente1.D2/SDA, U1.IN1
  N4: Componente1.D3_PWM/SCL, U1.IN2
  5V: Componente1.5V, U1.VCC
  GND: Componente1.GND, U1.GND

notes:
  CONTROL DE RELAY CON ARDUINO LEONARDO Y ANDROID
  ARDUINO LEONARDO
  HC_06
  DOBLE RELAY

custom parts:
  2-Channel 5v Relay Shield: 2 Channel 5v Relay Shield w. 2x SPD-06VDC-SD-C
