# Fritzing sketch Control de 2 Relay con Arduino Nano (saved by Fritzing 0.9.3b)

parts:
  Componente1 = Arduino Nano (Rev3.0)
  U1 = 2-Channel 5v Relay Shield [package=relay-2ch5v10a]
  Componente2 = Bluetooth HC-05 Macho

nets:
  N1: Componente1.D1/TX, Componente2.RXD
  N2: Componente1.D0/RX, Componente2.TXD
  N3: Componente1.D3, U1.IN1
  N4: Componente1.D4, U1.IN2
  GND: Componente1.GND, U1.GND
  N5: Componente1.RESET, U1.VCC

notes:
  HC_06
  ARDUINO NANO
  RELY DOBLE

custom parts:
  2-Channel 5v Relay Shield: 2 Channel 5v Relay Shield w. 2x SPD-06VDC-SD-C
