# Fritzing sketch Control de 2 Relay con Arduino UNO (saved by Fritzing 0.9.3b)
circuit board: 8.46667cm x 5.64444cm

parts:
  Componente1 = Arduino Uno (Rev3)
  Componente2 = Bluetooth HC-05 Macho
  U2 = 2-Channel 5v Relay Shield [package=relay-2ch5v10a]

nets:
  N1: Componente1.D0/RX, Componente2.TXD
  N2: Componente1.D1/TX, Componente2.RXD
  N3: Componente1.D2, U2.IN1
  N4: Componente1.D3_PWM, U2.IN2
  5V: Componente1.5V, U2.VCC
  GND: Componente1.GND, U2.GND

notes:
  CONTROL DE RELAY CON ARDUINO UNO Y ANDROID
  DOBLE RELAY
  HC_06
  ARDUINO UNO

custom parts:
  2-Channel 5v Relay Shield: 2 Channel 5v Relay Shield w. 2x SPD-06VDC-SD-C
